// Logisim project SDDisplay.circ as structural Verilog: 4 circuits, main circuit main
module main (
);

  wire Botao___Sensor_out, carros_1_am, carros_1_ve, carros_1_vm, display_2_1_s0, display_2_1_s1,
       display_2_1_s2, display_2_1_s3, display_2_1_s4, display_2_1_s5, display_2_1_s6, peoes_1_am, peoes_1_p,
       peoes_1_ve, peoes_1_vm, peoes_1_x0, peoes_1_x1, peoes_1_x2, peoes_1_x3;

  Clock clock_1 ();  // open: out
  Button Botao___Sensor (.out(Botao___Sensor_out));
  Carros carros_1 (
    .Botao___Sensor(Botao___Sensor_out), .Peoes(peoes_1_p), .VM(carros_1_vm), .AM(carros_1_am),
    .VE(carros_1_ve));
  Peoes peoes_1 (
    .S(Botao___Sensor_out), .VM(peoes_1_vm), .AM(peoes_1_am), .x3(peoes_1_x3), .VE(peoes_1_ve),
    .X2(peoes_1_x2), .P(peoes_1_p), .X1(peoes_1_x1), .X0(peoes_1_x0));
  LED led_1 (.in(carros_1_vm));
  LED led_2 (.in(carros_1_am));
  LED led_3 (.in(carros_1_ve));
  LED led_4 (.in(peoes_1_vm));
  LED led_5 (.in(peoes_1_am));
  LED led_6 (.in(peoes_1_ve));
  Display_2 display_2_1 (
    .X3(peoes_1_x3), .X2(peoes_1_x2), .X1(peoes_1_x1), .X0(peoes_1_x0), .S0(display_2_1_s0),
    .S1(display_2_1_s1), .S2(display_2_1_s2), .S3(display_2_1_s3), .S4(display_2_1_s4), .S5(display_2_1_s5),
    .S6(display_2_1_s6));
  _7_Segment_Display u_7_segment_display_1 (
    .g(display_2_1_s6), .f(display_2_1_s5), .a(display_2_1_s0), .b(display_2_1_s1), .e(display_2_1_s4),
    .d(display_2_1_s3), .c(display_2_1_s2));  // open: dp
endmodule

module Peoes (
  input  S,
  output VM,
  output AM,
  output x3,
  output VE,
  output X2,
  output P,
  output X1,
  output X0
);

  wire and_2_out, and_3_out, and_4_out, and_5_out, and_6_out, and_7_out, and_8_out, and_9_out, and_11_out,
       and_12_out, and_13_out, and_14_out, and_15_out, and_16_out, and_17_out, and_18_out, clock_1_out,
       not_1_out, not_2_out, not_3_out, not_4_out, not_5_out, not_6_out, not_7_out, not_8_out, not_9_out,
       not_10_out, or_1_out, or_2_out, or_5_out, or_6_out;

  not not_1 (not_1_out, x3);
  not not_2 (not_2_out, X2);
  not not_3 (not_3_out, X1);
  not not_4 (not_4_out, x3);
  not not_5 (not_5_out, X2);
  and and_1 (P, x3, X2, X1);
  and and_2 (and_2_out, X2, X1, X0);
  and and_3 (and_3_out, X1, X0);
  not not_6 (not_6_out, x3);
  not not_7 (not_7_out, X2);
  not not_8 (not_8_out, X2);
  not not_9 (not_9_out, x3);
  not not_10 (not_10_out, X1);
  and and_4 (and_4_out, X2, X1);
  and and_5 (and_5_out, X1, X0);
  and and_6 (and_6_out, x3, X1);
  and and_7 (and_7_out, x3, X2);
  and and_8 (and_8_out, not_1_out, not_2_out);
  and and_9 (and_9_out, x3, X2, X1);
  and and_10 (AM, x3, X2, not_3_out);
  and and_11 (and_11_out, not_4_out, X2);
  and and_12 (and_12_out, x3, not_5_out);
  and and_13 (and_13_out, not_6_out, X0);
  and and_14 (and_14_out, not_7_out, X0);
  and and_15 (and_15_out, S, X0);
  and and_16 (and_16_out, not_8_out, X1);
  and and_17 (and_17_out, not_9_out, X2);
  and and_18 (and_18_out, x3, not_10_out);
  or or_1 (or_1_out, and_5_out, and_6_out);
  or or_2 (or_2_out, X0, and_7_out);
  or or_3 (VM, and_8_out, and_9_out);
  or or_4 (VE, and_11_out, and_12_out);
  or or_5 (or_5_out, and_13_out, and_14_out, and_15_out);
  Clock clock_1 (.out(clock_1_out));
  or or_6 (or_6_out, and_16_out, and_17_out, and_18_out);
  J_K_Flip_Flop JK3 (.J(and_2_out), .clk(clock_1_out), .K(and_4_out), .Q(x3));  // open: Qn, preset, en, reset
  J_K_Flip_Flop JK2 (.J(and_3_out), .clk(clock_1_out), .K(or_1_out), .Q(X2));  // open: Qn, preset, en, reset
  J_K_Flip_Flop JK1 (.J(or_5_out), .clk(clock_1_out), .K(or_2_out), .Q(X1));  // open: Qn, preset, en, reset
  J_K_Flip_Flop JK0 (.J(or_6_out), .clk(clock_1_out), .K(1'b1), .Q(X0));  // open: Qn, preset, en, reset
endmodule

module Carros (
  input  Botao___Sensor,
  input  Peoes,
  output VM,
  output AM,
  output VE
);

  wire and_1_out, clock_1_out, JK0_q, JK0_qn, JK1_q, JK1_qn, or_1_out, or_2_out;

  Clock clock_1 (.out(clock_1_out));
  and and_1 (and_1_out, Peoes, JK0_q);
  or or_1 (or_1_out, Botao___Sensor, JK1_q);
  or or_2 (or_2_out, JK1_qn, Peoes);
  J_K_Flip_Flop JK1 (.J(JK0_q), .clk(clock_1_out), .K(and_1_out), .Q(JK1_q), .Qn(JK1_qn));  // open: preset, en, reset
  J_K_Flip_Flop JK0 (.J(or_1_out), .clk(clock_1_out), .K(or_2_out), .Q(JK0_q), .Qn(JK0_qn));  // open: preset, en, reset
  and and_2 (VM, JK1_q, JK0_q);
  xor xor_1 (AM, JK1_q, JK0_q);
  and and_3 (VE, JK1_qn, JK0_qn);
endmodule

// Display
module Display_2 (
  input  X3,
  input  X2,
  input  X1,
  input  X0,
  output S0,
  output S1,
  output S2,
  output S3,
  output S4,
  output S5,
  output S6
);

  wire and_1_out, and_2_out, and_3_out, and_4_out, and_5_out, and_6_out, and_7_out, and_8_out, and_9_out,
       and_10_out, and_11_out, and_12_out, and_13_out, and_14_out, and_15_out, and_16_out, and_17_out,
       and_18_out, and_19_out, and_20_out, and_21_out, and_22_out, and_23_out, not_1_out, not_2_out,
       not_3_out, not_4_out, not_5_out, not_6_out, not_7_out, not_8_out, not_9_out, not_10_out, not_11_out,
       not_12_out, not_13_out, not_14_out, not_15_out, not_16_out, not_17_out, not_18_out, not_19_out,
       not_20_out, not_21_out, not_22_out, not_23_out, not_24_out, not_25_out, not_26_out, not_27_out,
       not_28_out, not_29_out, not_30_out, not_31_out, not_32_out, not_33_out, not_34_out, not_35_out,
       not_36_out, not_37_out, not_38_out, not_39_out, not_40_out, not_41_out, not_42_out, not_43_out,
       not_44_out, not_45_out, not_46_out, not_47_out, not_48_out, not_49_out, not_50_out, not_51_out;

  not not_1 (not_1_out, X3);
  and and_1 (and_1_out, not_1_out, not_2_out);
  not not_2 (not_2_out, X2);
  not not_3 (not_3_out, X2);
  and and_2 (and_2_out, not_3_out, not_4_out, not_5_out);
  not not_4 (not_4_out, X1);
  not not_5 (not_5_out, X0);
  not not_6 (not_6_out, X3);
  not not_7 (not_7_out, X1);
  and and_3 (and_3_out, not_6_out, not_7_out, X0);
  not not_8 (not_8_out, X3);
  and and_4 (and_4_out, not_8_out, X1, not_9_out);
  not not_9 (not_9_out, X0);
  not not_10 (not_10_out, X3);
  and and_5 (and_5_out, not_10_out, not_11_out);
  not not_11 (not_11_out, X1);
  not not_12 (not_12_out, X2);
  not not_13 (not_13_out, X1);
  and and_6 (and_6_out, not_12_out, not_13_out, not_14_out);
  not not_14 (not_14_out, X0);
  not not_15 (not_15_out, X3);
  and and_7 (and_7_out, not_15_out, X2);
  not not_16 (not_16_out, X3);
  and and_8 (and_8_out, not_16_out, not_17_out);
  not not_17 (not_17_out, X2);
  not not_18 (not_18_out, X3);
  and and_9 (and_9_out, not_18_out, not_19_out);
  not not_19 (not_19_out, X1);
  not not_20 (not_20_out, X2);
  not not_21 (not_21_out, X1);
  and and_10 (and_10_out, not_20_out, not_21_out, not_22_out);
  not not_22 (not_22_out, X0);
  not not_23 (not_23_out, X3);
  and and_11 (and_11_out, not_23_out, X0);
  not not_24 (not_24_out, X2);
  not not_25 (not_25_out, X1);
  not not_26 (not_26_out, X0);
  not not_27 (not_27_out, X3);
  not not_28 (not_28_out, X2);
  not not_29 (not_29_out, X3);
  not not_30 (not_30_out, X0);
  not not_31 (not_31_out, X3);
  not not_32 (not_32_out, X1);
  not not_33 (not_33_out, X2);
  and and_12 (and_12_out, not_33_out, not_34_out, not_35_out);
  not not_34 (not_34_out, X1);
  not not_35 (not_35_out, X0);
  not not_36 (not_36_out, X3);
  and and_13 (and_13_out, not_36_out, X1, not_37_out);
  not not_37 (not_37_out, X0);
  not not_38 (not_38_out, X3);
  and and_14 (and_14_out, not_38_out, not_39_out, not_40_out);
  not not_39 (not_39_out, X1);
  not not_40 (not_40_out, X0);
  not not_41 (not_41_out, X2);
  and and_15 (and_15_out, not_41_out, not_42_out, not_43_out);
  not not_42 (not_42_out, X1);
  not not_43 (not_43_out, X0);
  not not_44 (not_44_out, X3);
  and and_16 (and_16_out, not_44_out, not_45_out, X1);
  not not_45 (not_45_out, X2);
  not not_46 (not_46_out, X3);
  and and_17 (and_17_out, not_46_out, not_47_out);
  not not_47 (not_47_out, X0);
  not not_48 (not_48_out, X3);
  not not_49 (not_49_out, X2);
  and and_18 (and_18_out, not_48_out, not_49_out, X1);
  not not_50 (not_50_out, X3);
  and and_19 (and_19_out, not_50_out, X2, not_51_out);
  not not_51 (not_51_out, X1);
  or or_1 (S0, and_1_out, and_2_out, and_3_out, and_4_out);
  or or_2 (S1, and_5_out, and_6_out, and_7_out);
  or or_3 (S2, and_8_out, and_9_out, and_10_out, and_11_out);
  and and_20 (and_20_out, not_24_out, not_25_out, not_26_out);
  and and_21 (and_21_out, not_27_out, not_28_out, X1);
  and and_22 (and_22_out, not_29_out, X1, not_30_out);
  and and_23 (and_23_out, not_31_out, X2, not_32_out, X0);
  or or_4 (S4, and_12_out, and_13_out);
  or or_5 (S5, and_14_out, and_15_out, and_16_out);
  or or_6 (S6, and_17_out, and_18_out, and_19_out);
  or or_7 (S3, and_20_out, and_21_out, and_22_out, and_23_out);
endmodule
